# Fritzing sketch project kutip sawit diagram (saved by Fritzing 0.9.3b)

parts:
  Part1 = Arduino Mega 2560 (Rev3)
  J1 = shrouded pin header, 10 pins [form="♂ (shrouded male)"]  # not connected
  U1 = TRANSCHIPTC5747 [package=camera_sfv24r-2st_2]  # not connected
  Part2 = MDD10A
  U2 = 4-Channel 5v Relay Shield [package=relay-4ch5v10a]
  M1 = DC Motor
  M2 = DC Motor
  M3 = DC Motor
  M4 = DC Motor
  BULB2 = LEDs [package=led10mm]
  BULB1 = LEDs [package=led10mm]
  S1 = Toggle Switch [package=THT]
  BAT1 = Battery Holders [package=lipo-1100mAh]
  U3 = LM2596 step down module

nets:
  N1: Part1.D19/RX1, U2.IN2
  N2: Part1.D18/TX1, U2.IN1
  GND: Part1.GND, Part2.no_name_yet#connectorBatt-2, Part2.no_name_yet#connectorgnd-1, U2.GND, BULB2.A, BULB1.A, S1.COM, BAT1.-, U3.IN-, U3.OUT-
  N3: Part1.D8_PWM, S1.L2
  N4: Part1.VIN, U3.OUT+
  N5: Part1.D4_PWM, Part2.no_name_yet#connectordir-2
  N6: Part1.D5_PWM, Part2.no_name_yet#connectorpwm-2
  N7: Part1.D6_PWM, Part2.no_name_yet#connectorpwm-1
  N8: Part1.D7_PWM, Part2.no_name_yet#connectordir-1
  5V: Part1.5V, U2.VCC
  N9: Part2.no_name_yet#connectorBatt-1, BAT1.+, U3.IN+
  N10: Part2.no_name_yet#connectorM1A-1, M1.pin_1, M3.pin_1
  N11: Part2.no_name_yet#connectorM1B-1, M1.pin_2, M3.pin_2
  N12: Part2.no_name_yet#connectorM2A-1, M2.pin_2, M4.pin_2
  N13: Part2.no_name_yet#connectorM2B-1, M2.pin_1, M4.pin_1
  N14: U2.K3-Off, U2.K4-Off
  N15: U2.K3-On, BULB1.C
  N16: U2.K4-On, BULB2.C

custom parts:
  4-Channel 5v Relay Shield: 4 Channel 5v Relay Shield w. 2x SPD-06VDC-SD-C
  LM2596 step down module: LM2596 DC-DC step down power supply module 3 A.
